// Logisim project PLDs.circ as structural Verilog
module PC_BUS_PLD (
  input  t0,
  input  t2,
  output PC_BUS
);

  or or_1 (PC_BUS, t0, t2);
endmodule

module AR_LD_PLD (
  input  t0,
  input  t2,
  input  t4,
  input  clock,
  input  d1,
  input  d2,
  output AR_LD
);

  wire and_1_out, not_1_out, or_1_out, or_2_out;

  not not_1 (not_1_out, clock);
  or or_1 (or_1_out, d1, d2);
  and and_1 (and_1_out, t4, or_1_out);
  or or_2 (or_2_out, t0, t2, and_1_out);
  and and_2 (AR_LD, or_2_out, not_1_out);
endmodule

module PC_LD_PLD (
  input  t4,
  input  clock,
  input  d5,
  input  d6,
  input  z,
  output PC_LD
);

  wire and_1_out, not_1_out, or_1_out;

  not not_1 (not_1_out, clock);
  or or_1 (or_1_out, d5, and_1_out);
  and and_1 (and_1_out, d6, z);
  and and_2 (PC_LD, t4, or_1_out, not_1_out);
endmodule

module SBC_PC_INC0 (
  input  t1,
  input  t3,
  input  clock,
  input  d1,
  input  d2,
  output PC_INC0
);

  wire and_1_out, not_1_out, or_1_out, or_2_out;

  not not_1 (not_1_out, clock);
  and and_1 (and_1_out, t3, or_1_out);
  or or_1 (or_1_out, d1, d2);
  or or_2 (or_2_out, t1, and_1_out);
  and and_2 (PC_INC0, or_2_out, not_1_out);
endmodule

module SBC_PC_INC1 (
  input  t3,
  input  clock,
  input  d6,
  input  z,
  output PC_INC1
);

  wire not_1_out, not_2_out;

  not not_1 (not_1_out, clock);
  not not_2 (not_2_out, z);
  and and_1 (PC_INC1, t3, d6, not_2_out, not_1_out);
endmodule

module PC_INC_PLD (
  input  t1,
  input  t3,
  input  clock,
  input  d1,
  input  d2,
  input  d6,
  input  z,
  output PC_INC
);

  wire sbc_pc_inc0_1_pc_inc0, sbc_pc_inc1_1_pc_inc1;

  SBC_PC_INC0 sbc_pc_inc0_1 (.t1(t1), .t3(t3), .clock(clock), .d1(d1), .d2(d2), .PC_INC0(sbc_pc_inc0_1_pc_inc0));
  SBC_PC_INC1 sbc_pc_inc1_1 (.t3(t3), .clock(clock), .d6(d6), .z(z), .PC_INC1(sbc_pc_inc1_1_pc_inc1));
  or or_1 (PC_INC, sbc_pc_inc0_1_pc_inc0, sbc_pc_inc1_1_pc_inc1);
endmodule

module SBC_DR_LD0 (
  input  t1,
  input  t3,
  input  clock,
  input  d1,
  input  d2,
  input  d5,
  output DR_LD0
);

  wire and_1_out, not_1_out, or_1_out, or_2_out;

  not not_1 (not_1_out, clock);
  or or_1 (or_1_out, d1, d2, d5);
  and and_1 (and_1_out, t3, or_1_out);
  or or_2 (or_2_out, t1, and_1_out);
  and and_2 (DR_LD0, or_2_out, not_1_out);
endmodule

module SBC_DR_LD1 (
  input  t3,
  input  clock,
  input  d6,
  input  z,
  output DR_LD1
);

  wire not_1_out;

  not not_1 (not_1_out, clock);
  and and_1 (DR_LD1, d6, z, t3, not_1_out);
endmodule

module SBC_DR_LD2 (
  input  t5,
  input  clock,
  input  d1,
  input  d2,
  output DR_LD2
);

  wire not_1_out, or_1_out;

  not not_1 (not_1_out, clock);
  or or_1 (or_1_out, d1, d2);
  and and_1 (DR_LD2, t5, or_1_out, not_1_out);
endmodule

module DR_LD_PLD (
  input  t1,
  input  t3,
  input  t5,
  input  clock,
  input  d1,
  input  d2,
  input  d5,
  input  d6,
  input  z,
  output DR_LD
);

  wire sbc_dr_ld0_1_dr_ld0, sbc_dr_ld1_1_dr_ld1, sbc_dr_ld2_1_dr_ld2;

  SBC_DR_LD0 sbc_dr_ld0_1 (.t1(t1), .t3(t3), .clock(clock), .d1(d1), .d2(d2), .d5(d5), .DR_LD0(sbc_dr_ld0_1_dr_ld0));
  SBC_DR_LD1 sbc_dr_ld1_1 (.t3(t3), .clock(clock), .d6(d6), .z(z), .DR_LD1(sbc_dr_ld1_1_dr_ld1));
  SBC_DR_LD2 sbc_dr_ld2_1 (.t5(t5), .clock(clock), .d1(d1), .d2(d2), .DR_LD2(sbc_dr_ld2_1_dr_ld2));
  or or_1 (DR_LD, sbc_dr_ld0_1_dr_ld0, sbc_dr_ld1_1_dr_ld1, sbc_dr_ld2_1_dr_ld2);
endmodule

module SBC_DR_BUS0 (
  input  t4,
  input  d1,
  input  d2,
  input  d5,
  output DR_BUS0
);

  wire or_1_out;

  or or_1 (or_1_out, d1, d2, d5);
  and and_1 (DR_BUS0, t4, or_1_out);
endmodule

module SBC_DR_BUS1 (
  input  t4,
  input  t6,
  input  d1,
  input  d2,
  input  d6,
  input  z,
  output DR_BUS1
);

  wire and_1_out, and_2_out, or_1_out;

  or or_1 (or_1_out, d1, d2);
  and and_1 (and_1_out, d6, z, t4);
  and and_2 (and_2_out, t6, or_1_out);
  or or_2 (DR_BUS1, and_1_out, and_2_out);
endmodule

module DR_BUS_PLD (
  input  t4,
  input  t6,
  input  d1,
  input  d2,
  input  d5,
  input  d6,
  input  z,
  output DR_BUS
);

  wire sbc_dr_bus0_1_dr_bus0, sbc_dr_bus1_1_dr_bus1;

  SBC_DR_BUS0 sbc_dr_bus0_1 (.t4(t4), .d1(d1), .d2(d2), .d5(d5), .DR_BUS0(sbc_dr_bus0_1_dr_bus0));
  SBC_DR_BUS1 sbc_dr_bus1_1 (.t4(t4), .t6(t6), .d1(d1), .d2(d2), .d6(d6), .z(z), .DR_BUS1(sbc_dr_bus1_1_dr_bus1));
  or or_1 (DR_BUS, sbc_dr_bus0_1_dr_bus0, sbc_dr_bus1_1_dr_bus1);
endmodule

module R_LD_PLD (
  input  t3,
  input  clock,
  input  d3,
  output R_LD
);

  wire not_1_out;

  not not_1 (not_1_out, clock);
  and and_1 (R_LD, t3, d3, not_1_out);
endmodule

module R_BUS_PLD (
  input  t3,
  input  d4,
  input  d8,
  input  d9,
  input  d12,
  input  d13,
  output R_BUS
);

  wire or_1_out;

  and and_1 (R_BUS, t3, or_1_out);
  or or_1 (or_1_out, d4, d8, d9, d12, d13);
endmodule

module S_LD_PLD (
  input  t3,
  input  clock,
  input  d0,
  output S_LD
);

  wire not_1_out;

  not not_1 (not_1_out, clock);
  and and_1 (S_LD, t3, d0, not_1_out);
endmodule

module ACC_CLR_PLD (
  input  t3,
  input  d11,
  output ACC_CLR
);

  and and_1 (ACC_CLR, t3, d11);
endmodule

module SBC_ACC_LD0 (
  input  t3,
  input  clock,
  input  d4,
  input  d8,
  input  d9,
  input  d10,
  output ACC_LD0
);

  wire not_1_out, or_1_out;

  not not_1 (not_1_out, clock);
  or or_1 (or_1_out, d4, d8, d9, d10);
  and and_1 (ACC_LD0, t3, or_1_out, not_1_out);
endmodule

module SBC_ACC_LD1 (
  input  t3,
  input  clock,
  input  d12,
  input  d13,
  input  d14,
  input  d15,
  output ACC_LD1
);

  wire not_1_out, or_1_out;

  not not_1 (not_1_out, clock);
  or or_1 (or_1_out, d12, d13, d14, d15);
  and and_1 (ACC_LD1, t3, or_1_out, not_1_out);
endmodule

module SBC_ACC_LD2 (
  input  t6,
  input  clock,
  input  d1,
  output ACC_LD2
);

  wire not_1_out;

  not not_1 (not_1_out, clock);
  and and_1 (ACC_LD2, t6, d1, not_1_out);
endmodule

module ACC_LD_PLD (
  input  t3,
  input  t6,
  input  clock,
  input  d1,
  input  d4,
  input  d8,
  input  d9,
  input  d10,
  input  d12,
  input  d13,
  input  d14,
  input  d15,
  output ACC_LD
);

  wire sbc_acc_ld0_1_acc_ld0, sbc_acc_ld1_1_acc_ld1, sbc_acc_ld2_1_acc_ld2;

  SBC_ACC_LD0 sbc_acc_ld0_1 (
    .t3(t3), .clock(clock), .d4(d4), .d8(d8), .d9(d9), .d10(d10), .ACC_LD0(sbc_acc_ld0_1_acc_ld0));
  SBC_ACC_LD1 sbc_acc_ld1_1 (
    .t3(t3), .clock(clock), .d12(d12), .d13(d13), .d14(d14), .d15(d15), .ACC_LD1(sbc_acc_ld1_1_acc_ld1));
  SBC_ACC_LD2 sbc_acc_ld2_1 (.t6(t6), .clock(clock), .d1(d1), .ACC_LD2(sbc_acc_ld2_1_acc_ld2));
  or or_1 (ACC_LD, sbc_acc_ld0_1_acc_ld0, sbc_acc_ld1_1_acc_ld1, sbc_acc_ld2_1_acc_ld2);
endmodule

module ACC_BUS_PLD (
  input  t3,
  input  t5,
  input  d2,
  input  d3,
  input  d7,
  output ACC_BUS
);

  wire and_1_out, and_2_out, or_1_out;

  or or_1 (or_1_out, d3, d7);
  and and_1 (and_1_out, t3, or_1_out);
  and and_2 (and_2_out, t5, d2);
  or or_2 (ACC_BUS, and_1_out, and_2_out);
endmodule

module SBC_ALU_SEL0 (
  input  d1,
  input  d4,
  input  d9,
  input  d13,
  input  d15,
  output O0
);

  or or_1 (O0, d1, d4, d9, d13, d15);
endmodule

module SBC_ALU_SEL1 (
  input  d1,
  input  d4,
  input  d10,
  input  d14,
  input  d15,
  output O1
);

  or or_1 (O1, d1, d4, d10, d14, d15);
endmodule

module SBC_ALU_SEL2 (
  input  d12,
  input  d13,
  input  d14,
  input  d15,
  output O2
);

  or or_1 (O2, d12, d13, d14, d15);
endmodule

module ALU_SEL_PLD (
  input  d1,
  input  d4,
  input  d9,
  input  d10,
  input  d12,
  input  d13,
  input  d14,
  input  d15,
  output Sel_0,
  output Sel_1,
  output Sel_2
);

  SBC_ALU_SEL0 sbc_alu_sel0_1 (.d1(d1), .d4(d4), .d9(d9), .d13(d13), .d15(d15), .O0(Sel_0));
  SBC_ALU_SEL1 sbc_alu_sel1_1 (.d1(d1), .d4(d4), .d10(d10), .d14(d14), .d15(d15), .O1(Sel_1));
  SBC_ALU_SEL2 sbc_alu_sel2_1 (.d12(d12), .d13(d13), .d14(d14), .d15(d15), .O2(Sel_2));
endmodule

module Z_LD_PLD (
  input  in_1,
  output Z_LD
);


  assign Z_LD = in_1;
endmodule

module OUTR_LD_PLD (
  input  t3,
  input  clock,
  input  d7,
  output OUTR_LD
);

  wire not_1_out;

  not not_1 (not_1_out, clock);
  and and_1 (OUTR_LD, t3, d7, not_1_out);
endmodule

module RAM_WE_PLD (
  input  t6,
  input  clock,
  input  d2,
  output RAM_WE
);

  wire not_1_out;

  not not_1 (not_1_out, clock);
  and and_1 (RAM_WE, t6, d2, not_1_out);
endmodule

module SBC_RAM_OE0 (
  input  t1,
  input  t3,
  input  clock,
  input  d1,
  input  d2,
  input  d5,
  output RAM_OE0
);

  wire and_1_out, not_1_out, or_1_out, or_2_out;

  not not_1 (not_1_out, clock);
  or or_1 (or_1_out, d1, d2, d5);
  and and_1 (and_1_out, t3, or_1_out);
  or or_2 (or_2_out, t1, and_1_out);
  and and_2 (RAM_OE0, or_2_out, not_1_out);
endmodule

module SBC_RAM_OE1 (
  input  t3,
  input  t5,
  input  clock,
  input  d1,
  input  d6,
  input  z,
  output RAM_OE1
);

  wire and_1_out, and_2_out, not_1_out, or_1_out;

  not not_1 (not_1_out, clock);
  and and_1 (and_1_out, d6, z, t3);
  and and_2 (and_2_out, t5, d1);
  or or_1 (or_1_out, and_1_out, and_2_out);
  and and_3 (RAM_OE1, or_1_out, not_1_out);
endmodule

module RAM_OE_PLD (
  input  t1,
  input  t3,
  input  t5,
  input  clock,
  input  d1,
  input  d2,
  input  d5,
  input  d6,
  input  z,
  output RAM_OE
);

  wire sbc_ram_oe0_1_ram_oe0, sbc_ram_oe1_1_ram_oe1;

  SBC_RAM_OE0 sbc_ram_oe0_1 (
    .t1(t1), .t3(t3), .clock(clock), .d1(d1), .d2(d2), .d5(d5), .RAM_OE0(sbc_ram_oe0_1_ram_oe0));
  SBC_RAM_OE1 sbc_ram_oe1_1 (.t3(t3), .t5(t5), .clock(clock), .d1(d1), .d6(d6), .z(z), .RAM_OE1(sbc_ram_oe1_1_ram_oe1));
  or or_1 (RAM_OE, sbc_ram_oe0_1_ram_oe0, sbc_ram_oe1_1_ram_oe1);
endmodule

module IR_LD_PLD (
  input  t2,
  input  clock,
  output RAM_OE
);

  wire not_1_out;

  not not_1 (not_1_out, clock);
  and and_1 (RAM_OE, t2, not_1_out);
endmodule

module SBC_SC_CLR0 (
  input  t4,
  input  d3,
  input  d4,
  input  d6,
  input  d7,
  input  z,
  output SC_CLR0
);

  wire and_1_out, not_1_out, or_1_out;

  not not_1 (not_1_out, z);
  and and_1 (and_1_out, d6, not_1_out);
  or or_1 (or_1_out, d3, d4, and_1_out, d7);
  and and_2 (SC_CLR0, t4, or_1_out);
endmodule

module SBC_SC_CLR1 (
  input  t4,
  input  d8,
  input  d9,
  input  d10,
  input  d11,
  output SC_CLR1
);

  wire or_1_out;

  or or_1 (or_1_out, d8, d9, d10, d11);
  and and_1 (SC_CLR1, t4, or_1_out);
endmodule

module SBC_SC_CLR2 (
  input  t4,
  input  d12,
  input  d13,
  input  d14,
  input  d15,
  output SC_CLR2
);

  wire or_1_out;

  or or_1 (or_1_out, d12, d13, d14, d15);
  and and_1 (SC_CLR2, t4, or_1_out);
endmodule

module SBC_SC_CLR3 (
  input  t5,
  input  t7,
  input  d5,
  input  d6,
  input  z,
  output SC_CLR3
);

  wire and_1_out, and_2_out, or_1_out;

  and and_1 (and_1_out, d6, z);
  or or_1 (or_1_out, d5, and_1_out);
  and and_2 (and_2_out, t5, or_1_out);
  or or_2 (SC_CLR3, and_2_out, t7);
endmodule

module SC_CLR_PLD (
  input  t4,
  input  t5,
  input  t7,
  input  d3,
  input  d4,
  input  d5,
  input  d6,
  input  d7,
  input  d8,
  input  d9,
  input  d10,
  input  d11,
  input  d12,
  input  d13,
  input  d14,
  input  d15,
  input  z,
  output SC_CLR
);

  wire sbc_sc_clr0_1_sc_clr0, sbc_sc_clr1_1_sc_clr1, sbc_sc_clr2_1_sc_clr2, sbc_sc_clr3_1_sc_clr3;

  SBC_SC_CLR0 sbc_sc_clr0_1 (.t4(t4), .d3(d3), .d4(d4), .d6(d6), .d7(d7), .z(z), .SC_CLR0(sbc_sc_clr0_1_sc_clr0));
  SBC_SC_CLR1 sbc_sc_clr1_1 (.t4(t4), .d8(d8), .d9(d9), .d10(d10), .d11(d11), .SC_CLR1(sbc_sc_clr1_1_sc_clr1));
  SBC_SC_CLR2 sbc_sc_clr2_1 (.t4(t4), .d12(d12), .d13(d13), .d14(d14), .d15(d15), .SC_CLR2(sbc_sc_clr2_1_sc_clr2));
  SBC_SC_CLR3 sbc_sc_clr3_1 (.t5(t5), .t7(t7), .d5(d5), .d6(d6), .z(z), .SC_CLR3(sbc_sc_clr3_1_sc_clr3));
  or or_1 (SC_CLR, sbc_sc_clr0_1_sc_clr0, sbc_sc_clr1_1_sc_clr1, sbc_sc_clr2_1_sc_clr2, sbc_sc_clr3_1_sc_clr3);
endmodule
