// Logisim project RSC.circ as structural Verilog: 10 circuits, main circuit Arith_U
module Arith_U (
  input  [31:0] A,
  input  [31:0] B,
  input  S1,
  input  S0,
  output [31:0] AU_out
);

  wire and_1_out, nor_1_out;
  wire [31:0] adder_1_out, multiplexer_1_out, not_1_out;

  assign not_1_out = ~B;  // NOT_Gate not_1, 32 bits wide
  nor nor_1 (nor_1_out, S1, S0);
  Adder #(.width(32)) adder_1 (.a(A), .b(multiplexer_1_out), .out(adder_1_out), .cin(nor_1_out));  // open: cout
  Multiplexer #(.select(2), .width(32)) multiplexer_1 (
    .in0(not_1_out), .in1(B), .in2(32'h1), .in3(B), .out(multiplexer_1_out), .sel({S1, S0}));
  Multiplexer #(.width(32)) multiplexer_2 (.in0(adder_1_out), .in1(multiplexer_1_out), .out(AU_out), .sel(and_1_out));
  and and_1 (and_1_out, S1, S0);
endmodule

module Logic_U (
  input  [31:0] A,
  input  [31:0] B,
  input  S1,
  input  S0,
  output [31:0] Logic_Out
);

  wire [31:0] and_1_out, not_1_out, or_1_out, shifter_1_out;

  assign and_1_out = A & B;  // AND_Gate and_1, 32 bits wide
  assign or_1_out = A | B;  // OR_Gate or_1, 32 bits wide
  Shifter #(.shift("ar"), .width(32)) shifter_1 (.in(A), .\dist (5'b00001), .out(shifter_1_out));
  assign not_1_out = ~A;  // NOT_Gate not_1, 32 bits wide
  Multiplexer #(.select(2), .width(32)) multiplexer_1 (
    .in0(and_1_out), .in1(or_1_out), .in2(shifter_1_out), .in3(not_1_out), .out(Logic_Out), .sel({S1, S0}));
endmodule

module ALU (
  input  [31:0] A,
  input  [31:0] B,
  input  S2,
  input  S1,
  input  S0,
  output [31:0] ALU_Out
);

  wire [31:0] arith_u_1_au_out, logic_u_1_logic_out;

  Multiplexer #(.width(32)) multiplexer_1 (.in0(arith_u_1_au_out), .in1(logic_u_1_logic_out), .out(ALU_Out), .sel(S2));
  Arith_U arith_u_1 (.A(A), .B(B), .S1(S1), .S0(S0), .AU_out(arith_u_1_au_out));
  Logic_U logic_u_1 (.A(A), .B(B), .S1(S1), .S0(S0), .Logic_Out(logic_u_1_logic_out));
endmodule

module SC (
  input  Clock,
  input  Clear,
  output [2:0] SEQ_out
);

  wire [2:0] adder_1_out;

  Register #(.width(3)) register_1 (.D(adder_1_out), .clk(Clock), .Q(SEQ_out), .clr(Clear));  // open: en
  Adder #(.width(3)) adder_1 (.a(SEQ_out), .b(3'b001), .out(adder_1_out));  // open: cin, cout
endmodule

module DecoderCircuit (
  input  [31:0] IR_In,
  output [15:0] D_Out,
  output [3:0] Debug_Instruction
);

  wire or_2_out;
  wire [3:0] or_1_out;
  wire [15:0] decoder_1_out0;

  assign or_1_out = IR_In[7:4] | IR_In[11:8] | IR_In[15:12] | IR_In[19:16] | IR_In[23:20] | IR_In[27:24] | IR_In[31:28];  // OR_Gate or_1, 4 bits wide
  Decoder #(.enable("false"), .select(4)) decoder_1 (
    .out0(decoder_1_out0[0]), .out1(decoder_1_out0[1]), .out2(decoder_1_out0[2]), .out3(decoder_1_out0[3]),
    .out4(decoder_1_out0[4]), .out5(decoder_1_out0[5]), .out6(decoder_1_out0[6]), .out7(decoder_1_out0[7]),
    .out8(decoder_1_out0[8]), .out9(decoder_1_out0[9]), .out10(decoder_1_out0[10]),
    .out11(decoder_1_out0[11]), .out12(decoder_1_out0[12]), .out13(decoder_1_out0[13]),
    .out14(decoder_1_out0[14]), .out15(decoder_1_out0[15]), .sel(IR_In[3:0]));
  or or_2 (or_2_out, or_1_out[0], or_1_out[1], or_1_out[2], or_1_out[3]);
  Multiplexer #(.width(16)) multiplexer_1 (.in0(decoder_1_out0), .in1({16{1'b0}}), .out(D_Out), .sel(or_2_out));

  assign Debug_Instruction = IR_In[3:0];

  // Notes on the sheet:
  //   CLA 7
  //   Srush Fatah
endmodule

module TimerCircuit (
  input  Stop,
  input  Clock,
  input  Clear,
  output [7:0] T_Out
);

  wire [2:0] sc_1_seq_out;
  wire [7:0] decoder_1_out0;

  SC sc_1 (.Clock(Clock), .Clear(Clear), .SEQ_out(sc_1_seq_out));
  Decoder #(.enable("false"), .select(3)) decoder_1 (
    .out0(decoder_1_out0[0]), .out1(decoder_1_out0[1]), .out2(decoder_1_out0[2]), .out3(decoder_1_out0[3]),
    .out4(decoder_1_out0[4]), .out5(decoder_1_out0[5]), .out6(decoder_1_out0[6]), .out7(decoder_1_out0[7]),
    .sel(sc_1_seq_out));
  Multiplexer #(.width(8)) multiplexer_1 (.in0(decoder_1_out0), .in1({8{1'b0}}), .out(T_Out), .sel(Stop));

  // Notes on the sheet:
  //   CLA 7
  //   Srush Fatah
endmodule

module RSC (
  output [7:0] T,
  output [3:0] D
);

  wire control_1_acc_bus, control_1_acc_clr, control_1_acc_ld, control_1_ar_ld, control_1_dr_bus,
       control_1_dr_ld, control_1_ir_ld, control_1_outr_ld, control_1_pc_bus, control_1_pc_inc,
       control_1_pc_ld, control_1_r_bus, control_1_r_ld, control_1_ram_oe, control_1_ram_we, control_1_z_ld,
       Primary_Clock_out, z_reg_1_z_out;
  wire [2:0] control_1_alu_s;
  wire [31:0] acc_1_data_out, alu_1_alu_out, ar_1_data_out, dr_1_data_out, ir_1_data_out, outr_1_data_out,
       r_1_bus_out;

  Control control_1 (
    .Clock(Primary_Clock_out), .Z_In(z_reg_1_z_out), .IR_In(ir_1_data_out), .T(T), .IR_LD(control_1_ir_ld),
    .RAM_WE(control_1_ram_we), .RAM_OE(control_1_ram_oe), .D(D), .AR_LD(control_1_ar_ld),
    .PC_LD(control_1_pc_ld), .PC_INC(control_1_pc_inc), .PC_BUS(control_1_pc_bus), .DR_LD(control_1_dr_ld),
    .DR_BUS(control_1_dr_bus), .R_LD(control_1_r_ld), .R_BUS(control_1_r_bus), .ACC_LD(control_1_acc_ld),
    .ACC_CLR(control_1_acc_clr), .ACC_BUS(control_1_acc_bus), .ALU_S(control_1_alu_s),
    .OUTR_LD(control_1_outr_ld), .Z_LD(control_1_z_ld));
  Z_Reg z_reg_1 (.Clock(Primary_Clock_out), .Load(control_1_z_ld), .ACC_in(acc_1_data_out), .Z_out(z_reg_1_z_out));
  AR ar_1 (.Data_In(r_1_bus_out), .Clock(Primary_Clock_out), .Load(control_1_ar_ld), .Data_Out(ar_1_data_out));
  R r_1 (
    .Data_In(r_1_bus_out), .Load(control_1_r_ld), .Clock(Primary_Clock_out), .Bus_Enable(control_1_r_bus),
    .Bus_Out(r_1_bus_out));  // open: Data_Out
  ALU alu_1 (
    .A(acc_1_data_out), .B(r_1_bus_out), .S2(control_1_alu_s[0]), .S1(control_1_alu_s[1]),
    .S0(control_1_alu_s[2]), .ALU_Out(alu_1_alu_out));
  DR dr_1 (
    .Data_In(r_1_bus_out), .Load(control_1_dr_ld), .Clock(Primary_Clock_out), .Bus_Enable(control_1_dr_bus),
    .Data_Out(dr_1_data_out), .Bus_Out(r_1_bus_out));
  RAM #(.addrWidth(16), .dataWidth(32), .databus("bidir"), .trigger("high")) ram_1 (
    .addr(ar_1_data_out[15:0]), .we(control_1_ram_we), .oe(control_1_ram_oe), .data(r_1_bus_out));
  Clock Primary_Clock (.out(Primary_Clock_out));
  ACC acc_1 (
    .Data_In(alu_1_alu_out), .Load(control_1_acc_ld), .Clock(Primary_Clock_out), .Clear(control_1_acc_clr),
    .Bus_Enable(control_1_acc_bus), .Data_Out(acc_1_data_out), .Bus_Out(r_1_bus_out));
  OUTR outr_1 (.Data_In(r_1_bus_out), .Clock(Primary_Clock_out), .Load(control_1_outr_ld), .Data_Out(outr_1_data_out));
  PC pc_1 (
    .Data_In(r_1_bus_out), .Clock(Primary_Clock_out), .Bus_Enable(control_1_pc_bus),
    .Count(control_1_pc_inc), .Load(control_1_pc_ld), .Bus_Out(r_1_bus_out));  // open: Data_Out
  Hex_Digit_Display hex_digit_display_1 (.value(outr_1_data_out[31:28]));  // open: dp
  Hex_Digit_Display hex_digit_display_2 (.value(outr_1_data_out[27:24]));  // open: dp
  Hex_Digit_Display hex_digit_display_3 (.value(outr_1_data_out[23:20]));  // open: dp
  Hex_Digit_Display hex_digit_display_4 (.value(outr_1_data_out[19:16]));  // open: dp
  Hex_Digit_Display hex_digit_display_5 (.value(outr_1_data_out[15:12]));  // open: dp
  IR ir_1 (.Data_In(dr_1_data_out), .Clock(Primary_Clock_out), .Load(control_1_ir_ld), .Data_Out(ir_1_data_out));
  Hex_Digit_Display hex_digit_display_6 (.value(outr_1_data_out[11:8]));  // open: dp
  Hex_Digit_Display hex_digit_display_7 (.value(outr_1_data_out[7:4]));  // open: dp
  Hex_Digit_Display hex_digit_display_8 (.value(outr_1_data_out[3:0]));  // open: dp
endmodule

module Z_Reg (
  input  Clock,
  input  Load,
  input  [31:0] ACC_in,
  output Z_out
);

  wire nor_1_out;

  nor nor_1 (nor_1_out, ACC_in[0], ACC_in[1], ACC_in[2], ACC_in[3], ACC_in[4], ACC_in[5], ACC_in[6], ACC_in[7], ACC_in[8], ACC_in[9], ACC_in[10], ACC_in[11], ACC_in[12], ACC_in[13], ACC_in[14], ACC_in[15], ACC_in[16], ACC_in[17], ACC_in[18], ACC_in[19], ACC_in[20], ACC_in[21], ACC_in[22], ACC_in[23], ACC_in[24], ACC_in[25], ACC_in[26], ACC_in[27], ACC_in[28], ACC_in[29], ACC_in[30], ACC_in[31]);
  Onebit_reg onebit_reg_1 (.Clock(Clock), .Data(nor_1_out), .Clear(1'b0), .Load(Load), .Data_Out(Z_out));
endmodule

module Control (
  input  Clock,
  input  Z_In,
  input  [31:0] IR_In,
  output [7:0] T,
  output IR_LD,
  output RAM_WE,
  output RAM_OE,
  output [3:0] D,
  output AR_LD,
  output PC_LD,
  output PC_INC,
  output PC_BUS,
  output DR_LD,
  output DR_BUS,
  output R_LD,
  output R_BUS,
  output ACC_LD,
  output ACC_CLR,
  output ACC_BUS,
  output [2:0] ALU_S,
  output OUTR_LD,
  output Z_LD
);

  wire s_ld_pld_1_s_ld, s_reg_1_data_out, sc_clr_pld_1_sc_clr;
  wire [15:0] decodercircuit_1_d_out;

  S_Reg s_reg_1 (.Clock(Clock), .Data(1'b1), .Clear(1'b0), .Load(s_ld_pld_1_s_ld), .Data_Out(s_reg_1_data_out));
  TimerCircuit timercircuit_1 (.Stop(s_reg_1_data_out), .Clock(Clock), .Clear(sc_clr_pld_1_sc_clr), .T_Out(T));
  DecoderCircuit decodercircuit_1 (.IR_In(IR_In), .D_Out(decodercircuit_1_d_out), .Debug_Instruction(D));
  S_LD_PLD s_ld_pld_1 (.t3(T[3]), .clock(Clock), .d0(decodercircuit_1_d_out[0]), .S_LD(s_ld_pld_1_s_ld));
  SC_CLR_PLD sc_clr_pld_1 (
    .t4(T[4]), .t5(T[5]), .t7(T[7]), .d3(decodercircuit_1_d_out[3]), .d4(decodercircuit_1_d_out[4]),
    .d5(decodercircuit_1_d_out[5]), .d6(decodercircuit_1_d_out[6]), .d7(decodercircuit_1_d_out[7]),
    .d8(decodercircuit_1_d_out[8]), .d9(decodercircuit_1_d_out[9]), .d10(decodercircuit_1_d_out[10]),
    .d11(decodercircuit_1_d_out[11]), .d12(decodercircuit_1_d_out[12]), .d13(decodercircuit_1_d_out[13]),
    .d14(decodercircuit_1_d_out[14]), .d15(decodercircuit_1_d_out[15]), .z(Z_In), .SC_CLR(sc_clr_pld_1_sc_clr));
  IR_LD_PLD ir_ld_pld_1 (.t2(T[2]), .clock(Clock), .RAM_OE(IR_LD));
  RAM_WE_PLD ram_we_pld_1 (.t6(T[6]), .clock(Clock), .d2(decodercircuit_1_d_out[2]), .RAM_WE(RAM_WE));
  RAM_OE_PLD ram_oe_pld_1 (
    .t1(T[1]), .t3(T[3]), .t5(T[5]), .clock(Clock), .d1(decodercircuit_1_d_out[1]),
    .d2(decodercircuit_1_d_out[2]), .d5(decodercircuit_1_d_out[5]), .d6(decodercircuit_1_d_out[6]), .z(Z_In),
    .RAM_OE(RAM_OE));
  AR_LD_PLD ar_ld_pld_1 (
    .t0(T[0]), .t2(T[2]), .t4(T[4]), .clock(Clock), .d1(decodercircuit_1_d_out[1]),
    .d2(decodercircuit_1_d_out[2]), .AR_LD(AR_LD));
  PC_LD_PLD pc_ld_pld_1 (
    .t4(T[4]), .clock(Clock), .d5(decodercircuit_1_d_out[5]), .d6(decodercircuit_1_d_out[6]), .z(Z_In),
    .PC_LD(PC_LD));
  PC_INC_PLD pc_inc_pld_1 (
    .t1(T[1]), .t3(T[3]), .clock(Clock), .d1(decodercircuit_1_d_out[1]), .d2(decodercircuit_1_d_out[2]),
    .d6(decodercircuit_1_d_out[6]), .z(Z_In), .PC_INC(PC_INC));
  PC_BUS_PLD pc_bus_pld_1 (.t0(T[0]), .t2(T[2]), .PC_BUS(PC_BUS));
  DR_LD_PLD dr_ld_pld_1 (
    .t1(T[1]), .t3(T[3]), .t5(T[5]), .clock(Clock), .d1(decodercircuit_1_d_out[1]),
    .d2(decodercircuit_1_d_out[2]), .d5(decodercircuit_1_d_out[5]), .d6(decodercircuit_1_d_out[6]), .z(Z_In),
    .DR_LD(DR_LD));
  DR_BUS_PLD dr_bus_pld_1 (
    .t4(T[4]), .t6(T[6]), .d1(decodercircuit_1_d_out[1]), .d2(decodercircuit_1_d_out[2]),
    .d5(decodercircuit_1_d_out[5]), .d6(decodercircuit_1_d_out[6]), .z(Z_In), .DR_BUS(DR_BUS));
  R_LD_PLD r_ld_pld_1 (.t3(T[2]), .clock(Clock), .d3(decodercircuit_1_d_out[3]), .R_LD(R_LD));
  R_BUS_PLD r_bus_pld_1 (
    .t3(T[3]), .d4(decodercircuit_1_d_out[4]), .d8(decodercircuit_1_d_out[8]),
    .d9(decodercircuit_1_d_out[9]), .d12(decodercircuit_1_d_out[12]), .d13(decodercircuit_1_d_out[13]),
    .R_BUS(R_BUS));
  ACC_LD_PLD acc_ld_pld_1 (
    .t3(T[3]), .t6(T[6]), .clock(Clock), .d1(decodercircuit_1_d_out[1]), .d4(decodercircuit_1_d_out[4]),
    .d8(decodercircuit_1_d_out[8]), .d9(decodercircuit_1_d_out[9]), .d10(decodercircuit_1_d_out[10]),
    .d12(decodercircuit_1_d_out[12]), .d13(decodercircuit_1_d_out[13]), .d14(decodercircuit_1_d_out[14]),
    .d15(decodercircuit_1_d_out[15]), .ACC_LD(ACC_LD));
  ACC_CLR_PLD acc_clr_pld_1 (.t3(T[3]), .d11(decodercircuit_1_d_out[11]), .ACC_CLR(ACC_CLR));
  ACC_BUS_PLD acc_bus_pld_1 (
    .t3(T[3]), .t5(T[5]), .d2(decodercircuit_1_d_out[2]), .d3(decodercircuit_1_d_out[3]),
    .d7(decodercircuit_1_d_out[7]), .ACC_BUS(ACC_BUS));
  ALU_SEL_PLD alu_sel_pld_1 (
    .d1(decodercircuit_1_d_out[1]), .d4(decodercircuit_1_d_out[4]), .d9(decodercircuit_1_d_out[9]),
    .d10(decodercircuit_1_d_out[10]), .d12(decodercircuit_1_d_out[12]), .d13(decodercircuit_1_d_out[13]),
    .d14(decodercircuit_1_d_out[14]), .d15(decodercircuit_1_d_out[15]), .Sel_0(ALU_S[0]), .Sel_1(ALU_S[1]),
    .Sel_2(ALU_S[2]));
  OUTR_LD_PLD outr_ld_pld_1 (.t3(T[3]), .clock(Clock), .d7(decodercircuit_1_d_out[7]), .OUTR_LD(OUTR_LD));
  Z_LD_PLD z_ld_pld_1 (.in_1(1'b1), .Z_LD(Z_LD));
endmodule

module S_Reg (
  input  Clock,
  input  Data,
  input  Clear,
  input  Load,
  output Data_Out
);

  wire and_1_out, and_2_out, not_1_out;

  not not_1 (not_1_out, Data);
  J_K_Flip_Flop j_k_ff_1 (
    .J(and_1_out), .K(and_2_out), .clk(Clock), .Q(Data_Out), .preset(1'b0), .reset(Clear));  // open: Qn
  and and_1 (and_1_out, Data, Load);
  and and_2 (and_2_out, not_1_out, Load);
endmodule
